// Digital circuit Lab02.dig as structural Verilog
module Lab02 (
  input  B,
  input  C,
  input  A,
  input  D,
  output Fa,
  output Fb,
  output Fc,
  output Fd,
  output Fe,
  output Fg,
  output Ff
);

  wire AB, AC, ADnB, ADnC, AnB, AnBnC, AnC, BC, BCnD, BD, BDnA, BDnC, BnA, BnAnC, BnAnD, BnC, BnD, CD, CDnA,
       CnA, CnAnB, CnB, CnD, DnA, DnB, DnC, nA, nAnB, nAnBnD, nAnC, nAnCnD, nB, nBnD, nC, nCnD, nD;

  not not_1 (nA, A);
  not not_2 (nB, B);
  not not_3 (nC, C);
  not not_4 (nD, D);
  and and_1 (CnD, C, nD);
  and and_2 (CnB, C, nB);
  and and_3 (DnB, D, nB);
  and and_4 (nAnC, nA, nC);
  and and_5 (nBnD, nB, nD);
  and and_6 (CD, C, D);
  and and_7 (BC, C, B);
  and and_8 (AnC, A, nC);
  and and_9 (DnC, D, nC);
  and and_10 (CnA, C, nA);
  and and_11 (AB, A, B);
  and and_12 (BD, D, B);
  and and_13 (nCnD, nC, nD);
  and and_14 (nAnB, nA, nB);
  and and_15 (BnD, nD, B);
  and and_16 (BnA, nA, B);
  and and_17 (AnB, A, nB);
  and and_18 (DnA, nA, D);
  and and_19 (AC, C, A);
  and and_20 (BnC, B, nC);
  and and_21 (AnBnC, A, nB, nC);
  and and_22 (BDnA, nA, B, D);
  and and_23 (nAnCnD, nA, nC, nD);
  and and_24 (ADnC, A, nC, D);
  and and_25 (CDnA, nA, C, D);
  and and_26 (ADnB, A, nB, D);
  and and_27 (BDnC, nC, B, D);
  and and_28 (nAnBnD, nA, nB, nD);
  and and_29 (BCnD, C, B, nD);
  and and_30 (CnAnB, nA, nB, C);
  and and_31 (BnAnC, nA, B, nC);
  and and_32 (BnAnD, nA, B, nD);
  or or_1 (Fa, CnA, BC, nBnD, BDnA, AnBnC);
  or or_2 (Fb, nAnB, nBnD, nAnCnD, ADnC, CDnA);
  or or_3 (Fc, nAnC, BnA, DnC, AnB, DnA);
  or or_4 (Fd, AnC, ADnB, BDnC, nAnBnD, BCnD, CnAnB);
  or or_5 (Fe, CnD, AB, nBnD, AC);
  or or_6 (Ff, AC, AnB, BnAnC, BnAnD, nAnCnD);
  or or_7 (Fg, A, BnC, CnD, CnB);
  Seven_Seg seven_seg_1 (.a(Fa), .b(Fb), .c(Fc), .d(Fd), .e(Fe), .f(Ff), .g(Fg), .dp(1'b0));
endmodule
